// Logisim project L20 Computer.circ as structural Verilog
module main (
  input  [6:0] Debug_Addr,
  input  Reset
);

  wire and_1_out, and_2_out, and_3_out, and_4_out, and_5_out, and_7_out, C_q, Clock_out,
       conditionallogic_1_execute, decoder_1_out0, decoder_2_out0, decoder_2_out1, decoder_2_out2,
       decoder_2_out3, decoder_2_out4, decoder_2_out5, decoder_2_out6, decoder_2_out7, decoder_2_out8,
       decoder_2_out9, decoder_2_out10, decoder_2_out11, F_E_q, interruptcontroller_1_handle, N_q, not_1_out,
       or_1_out, or_2_out, or_3_out, or_4_out, V_q, Z_q;
  wire [1:0] interruptcontroller_1_type;
  wire [3:0] ALU_v, Register_File_debug_out_2, Register_File_debug_out_3, Register_File_debug_out_4,
       Register_File_debug_out_5, Register_File_debug_out_6, Register_File_debug_out_7;
  wire [7:0] FlagControl_flags_out;
  wire [7:4] rom_1_data_2;
  wire [23:0] adder_1_out, adder_2_out, bit_extender_1_out, PC_q, Register_File_pc_out, Register_File_sp_out,
       rom_1_data, SP_q;
  wire [23:20] rom_1_data_3;
  wire [31:0] ALU_result, data_in_src_1_data_out, ram_1_data, ram_2_data, Register_File_rd, Register_File_rm,
       Register_File_rn, shifter_1_data_out;
  wire [31:24] Register_File_debug_out;

  Adder #(.width(24)) adder_1 (.a(rom_1_data), .b(Register_File_pc_out), .out(adder_1_out));  // open: cin, cout
  Clock Clock (.out(Clock_out));
  and and_1 (and_1_out, Clock_out, ~decoder_1_out0);  // AND_Gate
  Decoder #(.select(2), .disabled(0)) decoder_1 (
    .out0(decoder_1_out0), .sel(interruptcontroller_1_type), .en(interruptcontroller_1_handle));  // open: out1, out2, out3
  and and_2 (and_2_out, ~and_7_out, not_1_out);  // AND_Gate
  not not_1 (not_1_out, F_E_q);
  Counter #(.width(1), .max('h1)) F_E (
    .count(and_1_out), .Q(F_E_q), .clk(and_1_out), .clr(Reset));  // open: load, D, carry
  and and_3 (and_3_out, not_1_out, decoder_2_out1);
  InterruptController interruptcontroller_1 (
    .Call_Clear(and_4_out), .InrCode({rom_1_data_2, rom_1_data[23:20]}), .Set(and_3_out),
    .Type(interruptcontroller_1_type), .Value(Register_File_rm), .Reset(Reset),
    .Handle(interruptcontroller_1_handle));  // open: Priority, HandleAddress
  and and_4 (and_4_out, decoder_2_out0, not_1_out);
  ROM #(.addrWidth(24), .dataWidth(32)) rom_1 (
    .addr(PC_q), .data({rom_1_data_3, rom_1_data_2, rom_1_data}));  // open: sel
  Counter #(.width(24), .max('hffffff), .ongoal("stay")) PC (
    .load(and_7_out), .D(adder_1_out), .count(and_2_out), .Q(PC_q), .clk(and_1_out), .clr(Reset));  // open: carry
  Adder #(.width(24)) adder_2 (.a(PC_q), .b(24'h2), .out(adder_2_out));  // open: cin, cout
  reg128 Register_File (
    .An(rom_1_data[20:14]), .Am(rom_1_data[6:0]), .Ad({rom_1_data_2, rom_1_data[23:21]}),
    .Data_In(data_in_src_1_data_out), .Debug_Addr(Debug_Addr), .Rn(Register_File_rn), .Rm(Register_File_rm),
    .Rd(Register_File_rd),
    .Debug_Out({Register_File_debug_out, Register_File_debug_out_2, Register_File_debug_out_3, Register_File_debug_out_4, Register_File_debug_out_5, Register_File_debug_out_6, Register_File_debug_out_7}),
    .Clock(and_1_out), .Reset(Reset), .WriteEn(or_2_out), .SP_In(SP_q), .SP_out(Register_File_sp_out),
    .PC_In(adder_2_out), .PC_out(Register_File_pc_out));
  Counter #(.width(24), .max('hffffff), .ongoal("stay")) SP (
    .load(decoder_2_out9), .D(Register_File_sp_out), .count(and_5_out), .Q(SP_q), .clk(and_5_out), .clr(Reset));  // open: carry
  and and_5 (and_5_out, F_E_q, or_1_out);
  or or_1 (or_1_out, decoder_2_out6, decoder_2_out9);
  or or_2 (or_2_out, decoder_2_out10, decoder_2_out9, or_4_out, decoder_2_out2);
  ALU ALU (
    .A(Register_File_rn), .B(Register_File_rm), .Result(ALU_result), .Carry_In(decoder_2_out7),
    .Control(decoder_2_out5), .N(ALU_v[3]), .Z(ALU_v[2]), .C(ALU_v[1]), .V(ALU_v[0]));
  or or_3 (or_3_out, decoder_2_out5, decoder_2_out4);
  Data_In_Src data_in_src_1 (
    .Memory_In(ram_2_data), .ALU_In(ALU_result), .Stack_In(ram_1_data), .Shift_In(shifter_1_data_out),
    .Data_Out(data_in_src_1_data_out), .M(decoder_2_out2), .ALU(or_4_out), .St(decoder_2_out9),
    .Sh(decoder_2_out10));
  Shifter shifter_1 (
    .Data_In(Register_File_rn), .RegShiftIn(Register_File_rm), .Imm12(rom_1_data[11:0]),
    .Imm5(rom_1_data[18:14]), .Data_Out(shifter_1_data_out), .Shift_Control(rom_1_data[13:12]));
  or or_4 (or_4_out, decoder_2_out5, decoder_2_out4);
  RAM #(.addrWidth(24), .dataWidth(32), .bus("separate")) ram_1 (
    .addr(SP_q), .din(Register_File_rn), .data(ram_1_data), .str(decoder_2_out6), .clk(F_E_q), .clr(Reset));  // open: sel, ld
  Decoder #(.select(4)) decoder_2 (
    .out0(decoder_2_out0), .out1(decoder_2_out1), .out2(decoder_2_out2), .out3(decoder_2_out3),
    .out4(decoder_2_out4), .out5(decoder_2_out5), .out6(decoder_2_out6), .out7(decoder_2_out7),
    .out8(decoder_2_out8), .out9(decoder_2_out9), .out10(decoder_2_out10), .out11(decoder_2_out11),
    .sel(rom_1_data_3));  // open: out12, out13, out14, out15, en
  FlagControl FlagControl (
    .Flags_in(ALU_v), .Mask(rom_1_data_2), .Flags_Out(FlagControl_flags_out), .ALU(or_3_out),
    .Clear(decoder_2_out8));  // open: Set
  and and_6 (decoder_2_out7, C_q, decoder_2_out4);
  ConditionalLogic conditionallogic_1 (
    .Condition(rom_1_data_2), .N(N_q), .Z(Z_q), .C(C_q), .V(V_q), .Execute(conditionallogic_1_execute));
  Bit_Extender #(.in_width(32), .out_width(24)) bit_extender_1 (.in(ALU_result), .out(bit_extender_1_out));
  Register #(.width(1)) N (
    .D(FlagControl_flags_out[6]), .en(FlagControl_flags_out[7]), .Q(N_q), .clk(and_1_out), .clr(Reset));
  and and_7 (and_7_out, conditionallogic_1_execute, decoder_2_out11);
  Register #(.width(1)) Z (
    .D(FlagControl_flags_out[4]), .en(FlagControl_flags_out[5]), .Q(Z_q), .clk(and_1_out), .clr(Reset));
  Hex_Digit_Display hex_digit_display_1 (.value(Register_File_debug_out[31:28]));  // open: dp
  Register #(.width(1)) V (
    .D(FlagControl_flags_out[0]), .en(FlagControl_flags_out[1]), .Q(V_q), .clk(and_1_out), .clr(Reset));
  Register #(.width(1)) C (
    .D(FlagControl_flags_out[2]), .en(FlagControl_flags_out[3]), .Q(C_q), .clk(and_1_out), .clr(Reset));
  RAM #(.addrWidth(24), .dataWidth(32), .bus("separate")) ram_2 (
    .addr(bit_extender_1_out), .din(Register_File_rd), .data(ram_2_data), .str(decoder_2_out3), .clk(F_E_q));  // open: sel, ld, clr
  Hex_Digit_Display hex_digit_display_2 (.value(Register_File_debug_out[27:24]));  // open: dp
  Hex_Digit_Display hex_digit_display_3 (.value(Register_File_debug_out_2));  // open: dp
  Hex_Digit_Display hex_digit_display_4 (.value(Register_File_debug_out_4));  // open: dp
  Hex_Digit_Display hex_digit_display_5 (.value(Register_File_debug_out_3));  // open: dp
  Hex_Digit_Display hex_digit_display_6 (.value(Register_File_debug_out_5));  // open: dp
  Hex_Digit_Display hex_digit_display_7 (.value(Register_File_debug_out_6));  // open: dp
  Hex_Digit_Display hex_digit_display_8 (.value(Register_File_debug_out_7));  // open: dp

  // Notes on the sheet:
  //   contents of rom_1 (hex, n*v repeats v):
  //   a0403100 a0e03100 a0608000 a080c001 a0a11001 a0c12001
endmodule

module reg32 (
  input  Reset,
  input  Clock,
  input  [31:0] Data_In,
  input  [4:0] An,
  input  [4:0] Am,
  input  [4:0] Rd,
  input  WriteEnable,
  input  [4:0] Ak,
  input  [4:0] DebugAddr,
  output [31:0] Rn,
  output [31:0] Rm,
  output [31:0] Rk,
  output [31:0] Debug_Out
);

  wire decoder_1_out0, decoder_1_out1, decoder_1_out2, decoder_1_out3, decoder_2_out0, decoder_2_out1,
       decoder_2_out2, decoder_2_out3, decoder_3_out0, decoder_3_out1, decoder_3_out2, decoder_3_out3,
       decoder_4_out0, decoder_4_out1, decoder_4_out2, decoder_4_out3, decoder_5_out0, decoder_5_out1,
       decoder_5_out2, decoder_5_out3, decoder_5_out4, decoder_5_out5, decoder_5_out6, decoder_5_out7,
       decoder_6_out0, decoder_6_out1, decoder_6_out2, decoder_6_out3, decoder_7_out0, decoder_7_out1,
       decoder_7_out2, decoder_7_out3, decoder_8_out0, decoder_8_out1, decoder_8_out2, decoder_8_out3,
       decoder_9_out0, decoder_9_out1, decoder_9_out2, decoder_9_out3;
  wire [31:0] multiplexer_2_out, multiplexer_3_out, multiplexer_4_out, multiplexer_5_out, multiplexer_6_out,
       multiplexer_7_out, multiplexer_8_out, multiplexer_9_out, register_1_q, register_2_q, register_3_q,
       register_4_q, register_5_q, register_6_q, register_7_q, register_8_q, register_9_q, register_10_q,
       register_11_q, register_12_q, register_13_q, register_14_q, register_15_q, register_16_q,
       register_17_q, register_18_q, register_19_q, register_20_q, register_21_q, register_22_q,
       register_23_q, register_24_q, register_25_q, register_26_q, register_27_q, register_28_q,
       register_29_q, register_30_q, register_31_q, register_32_q, undriven, undriven_2, undriven_3;

  Decoder #(.select(2), .disabled(0)) decoder_1 (
    .out0(decoder_1_out0), .out1(decoder_1_out1), .out2(decoder_1_out2), .out3(decoder_1_out3),
    .sel(Rd[4:3]), .en(decoder_5_out0));
  Register #(.width(32)) register_1 (.D(Data_In), .en(decoder_1_out0), .Q(register_1_q), .clk(Clock), .clr(Reset));
  Register #(.width(32)) register_2 (.D(undriven_2), .en(decoder_1_out1), .Q(register_2_q), .clk(Clock), .clr(Reset));
  Register #(.width(32)) register_3 (.D(undriven_3), .en(decoder_1_out2), .Q(register_3_q), .clk(Clock), .clr(Reset));
  Register #(.width(32)) register_4 (.D(undriven), .en(decoder_1_out3), .Q(register_4_q), .clk(Clock), .clr(Reset));
  Decoder #(.select(2), .disabled(0)) decoder_2 (
    .out0(decoder_2_out0), .out1(decoder_2_out1), .out2(decoder_2_out2), .out3(decoder_2_out3),
    .sel(Rd[4:3]), .en(decoder_5_out1));
  Register #(.width(32)) register_5 (.D(Data_In), .en(decoder_2_out0), .Q(register_5_q), .clk(Clock), .clr(Reset));
  Register #(.width(32)) register_6 (.D(undriven_2), .en(decoder_2_out1), .Q(register_6_q), .clk(Clock), .clr(Reset));
  Register #(.width(32)) register_7 (.D(undriven_3), .en(decoder_2_out2), .Q(register_7_q), .clk(Clock), .clr(Reset));
  Register #(.width(32)) register_8 (.D(undriven), .en(decoder_2_out3), .Q(register_8_q), .clk(Clock), .clr(Reset));
  Decoder #(.select(2), .disabled(0)) decoder_3 (
    .out0(decoder_3_out0), .out1(decoder_3_out1), .out2(decoder_3_out2), .out3(decoder_3_out3),
    .sel(Rd[4:3]), .en(decoder_5_out2));
  Register #(.width(32)) register_9 (.D(Data_In), .en(decoder_3_out0), .Q(register_9_q), .clk(Clock), .clr(Reset));
  Register #(.width(32)) register_10 (.D(undriven_2), .en(decoder_3_out1), .Q(register_10_q), .clk(Clock), .clr(Reset));
  Register #(.width(32)) register_11 (.D(undriven_3), .en(decoder_3_out2), .Q(register_11_q), .clk(Clock), .clr(Reset));
  Register #(.width(32)) register_12 (.D(undriven), .en(decoder_3_out3), .Q(register_12_q), .clk(Clock), .clr(Reset));
  Decoder #(.select(2), .disabled(0)) decoder_4 (
    .out0(decoder_4_out0), .out1(decoder_4_out1), .out2(decoder_4_out2), .out3(decoder_4_out3),
    .sel(Rd[4:3]), .en(decoder_5_out3));
  Decoder #(.select(3), .disabled(0)) decoder_5 (
    .out0(decoder_5_out0), .out1(decoder_5_out1), .out2(decoder_5_out2), .out3(decoder_5_out3),
    .out4(decoder_5_out4), .out5(decoder_5_out5), .out6(decoder_5_out6), .out7(decoder_5_out7),
    .sel(Rd[2:0]), .en(WriteEnable));
  Register #(.width(32)) register_13 (.D(Data_In), .en(decoder_4_out0), .Q(register_13_q), .clk(Clock), .clr(Reset));
  Register #(.width(32)) register_14 (.D(undriven_2), .en(decoder_4_out1), .Q(register_14_q), .clk(Clock), .clr(Reset));
  Register #(.width(32)) register_15 (.D(undriven_3), .en(decoder_4_out2), .Q(register_15_q), .clk(Clock), .clr(Reset));
  Register #(.width(32)) register_16 (.D(undriven), .en(decoder_4_out3), .Q(register_16_q), .clk(Clock), .clr(Reset));
  Decoder #(.select(2), .disabled(0)) decoder_6 (
    .out0(decoder_6_out0), .out1(decoder_6_out1), .out2(decoder_6_out2), .out3(decoder_6_out3),
    .sel(Rd[4:3]), .en(decoder_5_out4));
  Register #(.width(32)) register_17 (.D(Data_In), .en(decoder_6_out0), .Q(register_17_q), .clk(Clock), .clr(Reset));
  Register #(.width(32)) register_18 (.D(undriven_2), .en(decoder_6_out1), .Q(register_18_q), .clk(Clock), .clr(Reset));
  Register #(.width(32)) register_19 (.D(undriven_3), .en(decoder_6_out2), .Q(register_19_q), .clk(Clock), .clr(Reset));
  Register #(.width(32)) register_20 (.D(undriven), .en(decoder_6_out3), .Q(register_20_q), .clk(Clock), .clr(Reset));
  Decoder #(.select(2), .disabled(0)) decoder_7 (
    .out0(decoder_7_out0), .out1(decoder_7_out1), .out2(decoder_7_out2), .out3(decoder_7_out3),
    .sel(Rd[4:3]), .en(decoder_5_out5));
  Register #(.width(32)) register_21 (.D(Data_In), .en(decoder_7_out0), .Q(register_21_q), .clk(Clock), .clr(Reset));
  Register #(.width(32)) register_22 (.D(undriven_2), .en(decoder_7_out1), .Q(register_22_q), .clk(Clock), .clr(Reset));
  Register #(.width(32)) register_23 (.D(undriven_3), .en(decoder_7_out2), .Q(register_23_q), .clk(Clock), .clr(Reset));
  Register #(.width(32)) register_24 (.D(undriven), .en(decoder_7_out3), .Q(register_24_q), .clk(Clock), .clr(Reset));
  Decoder #(.select(2), .disabled(0)) decoder_8 (
    .out0(decoder_8_out0), .out1(decoder_8_out1), .out2(decoder_8_out2), .out3(decoder_8_out3),
    .sel(Rd[4:3]), .en(decoder_5_out6));
  Register #(.width(32)) register_25 (.D(Data_In), .en(decoder_8_out0), .Q(register_25_q), .clk(Clock), .clr(Reset));
  Register #(.width(32)) register_26 (.D(undriven_2), .en(decoder_8_out1), .Q(register_26_q), .clk(Clock), .clr(Reset));
  Register #(.width(32)) register_27 (.D(undriven_3), .en(decoder_8_out2), .Q(register_27_q), .clk(Clock), .clr(Reset));
  Register #(.width(32)) register_28 (.D(undriven), .en(decoder_8_out3), .Q(register_28_q), .clk(Clock), .clr(Reset));
  Decoder #(.select(2), .disabled(0)) decoder_9 (
    .out0(decoder_9_out0), .out1(decoder_9_out1), .out2(decoder_9_out2), .out3(decoder_9_out3),
    .sel(Rd[4:3]), .en(decoder_5_out7));
  Register #(.width(32)) register_29 (.D(Data_In), .en(decoder_9_out0), .Q(register_29_q), .clk(Clock), .clr(Reset));
  Register #(.width(32)) register_30 (.D(undriven_2), .en(decoder_9_out1), .Q(register_30_q), .clk(Clock), .clr(Reset));
  Register #(.width(32)) register_31 (.D(undriven_3), .en(decoder_9_out2), .Q(register_31_q), .clk(Clock), .clr(Reset));
  Register #(.width(32)) register_32 (.D(undriven), .en(decoder_9_out3), .Q(register_32_q), .clk(Clock), .clr(Reset));
  Multiplexer #(.select(5), .width(32)) multiplexer_1 (
    .in0(register_1_q), .in1(register_5_q), .in2(register_9_q), .in3(register_13_q), .in4(register_17_q),
    .in5(register_21_q), .in6(register_25_q), .in7(register_29_q), .in8(register_2_q), .in9(register_6_q),
    .in10(register_10_q), .in11(register_14_q), .in12(register_18_q), .in13(register_22_q),
    .in14(register_26_q), .in15(register_30_q), .in16(register_3_q), .in17(register_7_q),
    .in18(register_11_q), .in19(register_15_q), .in20(register_19_q), .in21(register_23_q),
    .in22(register_27_q), .in23(register_31_q), .in24(register_4_q), .in25(register_8_q),
    .in26(register_12_q), .in27(register_16_q), .in28(register_20_q), .in29(register_24_q),
    .in30(register_28_q), .in31(register_32_q), .out(Debug_Out), .sel(DebugAddr));  // open: en
  Multiplexer #(.select(3), .width(32)) multiplexer_2 (
    .in0(register_1_q), .in1(register_5_q), .in2(register_9_q), .in3(register_13_q), .in4(register_17_q),
    .in5(register_21_q), .in6(register_25_q), .in7(register_29_q), .out(multiplexer_2_out), .sel(An[2:0]));  // open: en
  Multiplexer #(.select(3), .width(32)) multiplexer_3 (
    .in0(register_1_q), .in1(register_5_q), .in2(register_9_q), .in3(register_13_q), .in4(register_17_q),
    .in5(register_21_q), .in6(register_25_q), .in7(register_29_q), .out(multiplexer_3_out), .sel(Am[2:0]));  // open: en
  Multiplexer #(.select(3), .width(32)) multiplexer_4 (
    .in0(register_2_q), .in1(register_6_q), .in2(register_10_q), .in3(register_14_q), .in4(register_18_q),
    .in5(register_22_q), .in6(register_26_q), .in7(register_30_q), .out(multiplexer_4_out), .sel(An[2:0]));  // open: en
  Multiplexer #(.select(3), .width(32)) multiplexer_5 (
    .in0(register_2_q), .in1(register_6_q), .in2(register_10_q), .in3(register_14_q), .in4(register_18_q),
    .in5(register_22_q), .in6(register_26_q), .in7(register_30_q), .out(multiplexer_5_out), .sel(Am[2:0]));  // open: en
  Multiplexer #(.select(3), .width(32)) multiplexer_6 (
    .in0(register_3_q), .in1(register_7_q), .in2(register_11_q), .in3(register_15_q), .in4(register_19_q),
    .in5(register_23_q), .in6(register_27_q), .in7(register_31_q), .out(multiplexer_6_out), .sel(An[2:0]));  // open: en
  Multiplexer #(.select(3), .width(32)) multiplexer_7 (
    .in0(register_3_q), .in1(register_7_q), .in2(register_11_q), .in3(register_15_q), .in4(register_19_q),
    .in5(register_23_q), .in6(register_27_q), .in7(register_31_q), .out(multiplexer_7_out), .sel(Am[2:0]));  // open: en
  Multiplexer #(.select(3), .width(32)) multiplexer_8 (
    .in0(register_4_q), .in1(register_8_q), .in2(register_12_q), .in3(register_16_q), .in4(register_20_q),
    .in5(register_24_q), .in6(register_28_q), .in7(register_32_q), .out(multiplexer_8_out), .sel(An[2:0]));  // open: en
  Multiplexer #(.select(3), .width(32)) multiplexer_9 (
    .in0(register_4_q), .in1(register_8_q), .in2(register_12_q), .in3(register_16_q), .in4(register_20_q),
    .in5(register_24_q), .in6(register_28_q), .in7(register_32_q), .out(multiplexer_9_out), .sel(Am[2:0]));  // open: en
  Multiplexer #(.select(5), .width(32)) multiplexer_10 (
    .in0(register_1_q), .in1(register_5_q), .in2(register_9_q), .in3(register_13_q), .in4(register_17_q),
    .in5(register_21_q), .in6(register_25_q), .in7(register_29_q), .in8(register_2_q), .in9(register_6_q),
    .in10(register_10_q), .in11(register_14_q), .in12(register_18_q), .in13(register_22_q),
    .in14(register_26_q), .in15(register_30_q), .in16(register_3_q), .in17(register_7_q),
    .in18(register_11_q), .in19(register_15_q), .in20(register_19_q), .in21(register_23_q),
    .in22(register_27_q), .in23(register_31_q), .in24(register_4_q), .in25(register_8_q),
    .in26(register_12_q), .in27(register_16_q), .in28(register_20_q), .in29(register_24_q),
    .in30(register_28_q), .in31(register_32_q), .out(Rk), .sel(Ak));  // open: en
  Multiplexer #(.select(2), .width(32)) multiplexer_11 (
    .in0(multiplexer_2_out), .in1(multiplexer_4_out), .in2(multiplexer_6_out), .in3(multiplexer_8_out),
    .out(Rn), .sel(An[4:3]));  // open: en
  Multiplexer #(.select(2), .width(32)) multiplexer_12 (
    .in0(multiplexer_3_out), .in1(multiplexer_5_out), .in2(multiplexer_7_out), .in3(multiplexer_9_out),
    .out(Rm), .sel(Am[4:3]));  // open: en
endmodule

module reg128 (
  input  Clock,
  input  Reset,
  input  WriteEn,
  input  [6:0] An,
  input  [6:0] Am,
  input  [6:0] Ad,
  input  [31:0] Data_In,
  input  [6:0] Debug_Addr,
  input  [23:0] SP_In,
  input  [23:0] PC_In,
  output [31:0] Rn,
  output [31:0] Rm,
  output [31:0] Rd,
  output [31:0] Debug_Out,
  output [23:0] SP_out,
  output [23:0] PC_out
);

  wire addresshelp_3_writable, and_1_out, and_2_out, and_3_out, decoder_1_out0, decoder_1_out1,
       decoder_1_out2, decoder_1_out3;
  wire [1:0] addresshelp_1_select, addresshelp_1_value, addresshelp_2_select, addresshelp_2_value,
       addresshelp_3_select, addresshelp_3_value, addresshelp_4_select, addresshelp_4_value;
  wire [31:0] bit_extender_1_out, bit_extender_2_out, bit_extender_5_out, bit_extender_6_out,
       bit_extender_7_out, bit_extender_8_out, multiplexer_1_out, multiplexer_2_out, multiplexer_3_out,
       multiplexer_4_out, multiplexer_5_out, multiplexer_6_out, reg32_1_debug_out, reg32_1_rk, reg32_1_rm,
       reg32_1_rn, reg32_2_debug_out, reg32_2_rk, reg32_2_rm, reg32_2_rn, reg32_3_debug_out, reg32_3_rk,
       reg32_3_rm, reg32_3_rn, reg32_4_debug_out, reg32_4_rk, reg32_4_rm, reg32_4_rn;

  AddressHelp addresshelp_1 (.Addr(An), .Value(addresshelp_1_value), .Select(addresshelp_1_select));  // open: Writable
  AddressHelp addresshelp_2 (.Addr(Am), .Value(addresshelp_2_value), .Select(addresshelp_2_select));  // open: Writable
  AddressHelp addresshelp_3 (
    .Addr(Ad), .Writable(addresshelp_3_writable), .Value(addresshelp_3_value), .Select(addresshelp_3_select));
  assign bit_extender_1_out = {{8{1'b0}}, SP_In};  // Bit_Extender bit_extender_1
  assign bit_extender_2_out = {{8{1'b0}}, PC_In};  // Bit_Extender bit_extender_2
  reg32 reg32_1 (
    .Rd(Ad[4:0]), .WriteEnable(decoder_1_out0), .DebugAddr(Debug_Addr[4:0]), .Rn(reg32_1_rn),
    .Rm(reg32_1_rm), .An(An[4:0]), .Am(Am[4:0]), .Rk(reg32_1_rk), .Ak(Ad[4:0]), .Reset(Reset), .Clock(Clock),
    .Debug_Out(reg32_1_debug_out), .Data_In(Data_In));
  reg32 reg32_2 (
    .Rd(Ad[4:0]), .WriteEnable(decoder_1_out1), .DebugAddr(Debug_Addr[4:0]), .Rn(reg32_2_rn),
    .Rm(reg32_2_rm), .An(An[4:0]), .Am(Am[4:0]), .Rk(reg32_2_rk), .Ak(Ad[4:0]), .Reset(Reset), .Clock(Clock),
    .Debug_Out(reg32_2_debug_out), .Data_In(Data_In));
  AddressHelp addresshelp_4 (
    .Addr(Debug_Addr), .Value(addresshelp_4_value), .Select(addresshelp_4_select));  // open: Writable
  and and_1 (and_1_out, addresshelp_3_writable, ~addresshelp_3_select[0], addresshelp_3_select[1]);  // AND_Gate
  and and_2 (and_2_out, addresshelp_3_writable, addresshelp_3_select[0], addresshelp_3_select[1]);
  and and_3 (and_3_out, WriteEn, addresshelp_3_writable);
  Decoder #(.select(2), .disabled(0)) decoder_1 (
    .out0(decoder_1_out0), .out1(decoder_1_out1), .out2(decoder_1_out2), .out3(decoder_1_out3),
    .sel(Ad[6:5]), .en(and_3_out));
  reg32 reg32_3 (
    .Rd(Ad[4:0]), .WriteEnable(decoder_1_out2), .DebugAddr(Debug_Addr[4:0]), .Rn(reg32_3_rn),
    .Rm(reg32_3_rm), .An(An[4:0]), .Am(Am[4:0]), .Rk(reg32_3_rk), .Ak(Ad[4:0]), .Reset(Reset), .Clock(Clock),
    .Debug_Out(reg32_3_debug_out), .Data_In(Data_In));
  Multiplexer #(.select(2), .width(32)) multiplexer_1 (
    .in0(reg32_1_debug_out), .in1(reg32_2_debug_out), .in2(reg32_3_debug_out), .in3(reg32_4_debug_out),
    .out(multiplexer_1_out), .sel(Debug_Addr[6:5]));  // open: en
  reg32 reg32_4 (
    .Rd(Ad[4:0]), .WriteEnable(decoder_1_out3), .DebugAddr(Debug_Addr[4:0]), .Rn(reg32_4_rn),
    .Rm(reg32_4_rm), .An(An[4:0]), .Am(Am[4:0]), .Rk(reg32_4_rk), .Ak(Ad[4:0]), .Reset(Reset), .Clock(Clock),
    .Debug_Out(reg32_4_debug_out), .Data_In(Data_In));
  Bit_Extender #(.in_width(32), .out_width(24)) bit_extender_3 (.in(multiplexer_2_out), .out(SP_out));
  Multiplexer #(.width(32)) multiplexer_2 (
    .in0(bit_extender_1_out), .in1(Data_In), .out(multiplexer_2_out), .sel(and_1_out));  // open: en
  Bit_Extender #(.in_width(32), .out_width(24)) bit_extender_4 (.in(multiplexer_3_out), .out(PC_out));
  Multiplexer #(.width(32)) multiplexer_3 (
    .in0(bit_extender_2_out), .in1(Data_In), .out(multiplexer_3_out), .sel(and_2_out));  // open: en
  assign bit_extender_5_out = {{30{addresshelp_4_value[1]}}, addresshelp_4_value};  // Bit_Extender bit_extender_5
  Multiplexer #(.select(2), .width(32)) multiplexer_4 (
    .in0(reg32_1_rn), .in1(reg32_2_rn), .in2(reg32_3_rn), .in3(reg32_4_rn), .out(multiplexer_4_out),
    .sel(An[6:5]));  // open: en
  Multiplexer #(.select(2), .width(32)) multiplexer_5 (
    .in0(reg32_1_rm), .in1(reg32_2_rm), .in2(reg32_3_rm), .in3(reg32_4_rm), .out(multiplexer_5_out),
    .sel(Am[6:5]));  // open: en
  Multiplexer #(.select(2), .width(32)) multiplexer_6 (
    .in0(reg32_1_rk), .in1(reg32_2_rk), .in2(reg32_3_rk), .in3(reg32_4_rk), .out(multiplexer_6_out),
    .sel(Ad[6:5]));  // open: en
  Multiplexer #(.select(2), .width(32)) multiplexer_7 (
    .in0(multiplexer_1_out), .in1(bit_extender_5_out), .in2(bit_extender_1_out), .in3(bit_extender_2_out),
    .out(Debug_Out), .sel(addresshelp_4_select));  // open: en
  assign bit_extender_6_out = {{30{addresshelp_1_value[1]}}, addresshelp_1_value};  // Bit_Extender bit_extender_6
  assign bit_extender_7_out = {{30{addresshelp_2_value[1]}}, addresshelp_2_value};  // Bit_Extender bit_extender_7
  assign bit_extender_8_out = {{30{addresshelp_3_value[1]}}, addresshelp_3_value};  // Bit_Extender bit_extender_8
  Multiplexer #(.select(2), .width(32)) multiplexer_8 (
    .in0(multiplexer_4_out), .in1(bit_extender_6_out), .in2(bit_extender_1_out), .in3(bit_extender_2_out),
    .out(Rn), .sel(addresshelp_1_select));  // open: en
  Multiplexer #(.select(2), .width(32)) multiplexer_9 (
    .in0(multiplexer_5_out), .in1(bit_extender_7_out), .in2(bit_extender_1_out), .in3(bit_extender_2_out),
    .out(Rm), .sel(addresshelp_2_select));  // open: en
  Multiplexer #(.select(2), .width(32)) multiplexer_10 (
    .in0(multiplexer_6_out), .in1(bit_extender_8_out), .in2(bit_extender_1_out), .in3(bit_extender_2_out),
    .out(Rd), .sel(addresshelp_3_select));  // open: en
endmodule

module ALU (
  input  Carry_In,
  input  Control,
  input  [31:0] A,
  input  [31:0] B,
  output [31:0] Result,
  output N,
  output Z,
  output C,
  output V
);

  wire adder_1_cout, and_2_out, not_1_out, xnor_1_out, xor_1_out;
  wire [31:0] adder_1_out, nand_1_out;

  nor nor_1 (Z, N, Result[30], Result[29], Result[28], Result[27], Result[26], Result[25], Result[24], Result[23], Result[22], Result[21], Result[20], Result[19], Result[18], Result[17], Result[16], Result[15], Result[14], Result[13], Result[12], Result[11], Result[10], Result[9], Result[8], Result[7], Result[6], Result[5], Result[4], Result[3], Result[2], Result[1], Result[0]);
  and and_1 (C, not_1_out, adder_1_cout);
  assign nand_1_out = ~(A & B);  // NAND_Gate nand_1, 32 bits wide
  Adder #(.width(32)) adder_1 (.a(A), .b(B), .out(adder_1_out), .cin(Carry_In), .cout(adder_1_cout));
  xor xor_1 (xor_1_out, A[31], N);
  xnor xnor_1 (xnor_1_out, A[31], B[31]);
  and and_2 (and_2_out, xnor_1_out, xor_1_out);
  and and_3 (V, and_2_out, not_1_out);
  not not_1 (not_1_out, Control);
  Multiplexer #(.width(32)) multiplexer_1 (
    .in0(nand_1_out), .in1(adder_1_out), .out({N, Result[30:0]}), .sel(not_1_out));  // open: en

  assign Result[31] = N;
endmodule

module FlagControl (
  input  [3:0] Flags_in,
  input  [3:0] Mask,
  input  ALU,
  input  Set,
  input  Clear,
  output [7:0] Flags_Out
);

  wire [1:0] priority_encoder_1_out;

  Priority_Encoder #(.select(2)) priority_encoder_1 (
    .in0(1'b1), .in1(ALU), .in2(Set), .in3(Clear), .out(priority_encoder_1_out));
  Multiplexer #(.select(2), .width(8)) multiplexer_1 (
    .in0({8{1'b0}}), .in1({1'b1, Flags_in[3], 1'b1, Flags_in[2], 1'b1, Flags_in[1], 1'b1, Flags_in[0]}),
    .in2({Mask[3], 1'b1, Mask[2], 1'b1, Mask[1], 1'b1, Mask[0], 1'b1}),
    .in3({Mask[3], 1'b0, Mask[2], 1'b0, Mask[1], 1'b0, Mask[0], 1'b0}), .out(Flags_Out),
    .sel(priority_encoder_1_out));  // open: en
endmodule

module Data_In_Src (
  input  [31:0] Memory_In,
  input  [31:0] ALU_In,
  input  [31:0] Stack_In,
  input  [31:0] Shift_In,
  input  M,
  input  ALU,
  input  St,
  input  Sh,
  output [31:0] Data_Out
);

  wire [1:0] priority_encoder_1_out;

  Multiplexer #(.select(2), .width(32)) multiplexer_1 (
    .in0(Memory_In), .in1(ALU_In), .in2(Stack_In), .in3(Shift_In), .out(Data_Out),
    .sel(priority_encoder_1_out));  // open: en
  Priority_Encoder #(.select(2)) priority_encoder_1 (
    .in0(M), .in1(ALU), .in2(St), .in3(Sh), .out(priority_encoder_1_out));
endmodule

module Shifter (
  input  [31:0] Data_In,
  input  [31:0] RegShiftIn,
  input  [11:0] Imm12,
  input  [4:0] Imm5,
  input  [1:0] Shift_Control,
  output [31:0] Data_Out
);

  wire [4:0] bit_extender_1_out;
  wire [31:0] bit_extender_2_out, shifter_1_out, shifter_2_out, shifter_3_out, shifter_4_out;

  Bit_Extender #(.in_width(32), .out_width(5)) bit_extender_1 (.in(RegShiftIn), .out(bit_extender_1_out));
  assign bit_extender_2_out = {{20{Imm12[11]}}, Imm12};  // Bit_Extender bit_extender_2
  Shifter_part #(.width(32)) shifter_1 (.in(Data_In), .\dist (bit_extender_1_out), .out(shifter_1_out));
  Shifter_part #(.width(32), .shift("lr")) shifter_2 (.in(Data_In), .\dist (bit_extender_1_out), .out(shifter_2_out));
  Shifter_part #(.width(32), .shift("ar")) shifter_3 (.in(Data_In), .\dist (bit_extender_1_out), .out(shifter_3_out));
  Shifter_part #(.width(32)) shifter_4 (.in(bit_extender_2_out), .\dist (Imm5), .out(shifter_4_out));
  Multiplexer #(.select(2), .width(32)) multiplexer_1 (
    .in0(shifter_1_out), .in1(shifter_2_out), .in2(shifter_3_out), .in3(shifter_4_out), .out(Data_Out),
    .sel(Shift_Control));  // open: en
endmodule

module AddressHelp (
  input  [6:0] Addr,
  output Writable,
  output [1:0] Value,
  output [1:0] Select
);

  wire and_1_out, and_2_out, and_4_out, and_5_out, and_6_out, not_1_out, not_2_out, or_1_out, or_2_out;

  or or_1 (or_1_out, Addr[6], Addr[5], Addr[4], Addr[3], Addr[2]);
  and and_1 (and_1_out, Addr[0], Addr[1]);
  and and_2 (and_2_out, Addr[2], Addr[3], Addr[4], Addr[5], Addr[6]);
  not not_1 (not_1_out, Writable);
  and and_3 (Writable, or_2_out, not_2_out);
  or or_2 (or_2_out, Addr[1], or_1_out);
  not not_2 (not_2_out, and_4_out);
  and and_4 (and_4_out, and_1_out, and_2_out);
  Priority_Encoder #(.select(2)) priority_encoder_1 (
    .in0(not_2_out), .in1(not_1_out), .in2(and_5_out), .in3(and_6_out), .out(Select));  // open: gs, en_out, en_in
  and and_5 (and_5_out, and_2_out, ~not_1_out, Addr[0]);  // AND_Gate
  and and_6 (and_6_out, Addr[1], ~not_1_out, and_2_out);  // AND_Gate

  assign Value = Addr[1:0];
endmodule

module ConditionalLogic (
  input  N,
  input  Z,
  input  C,
  input  V,
  input  [3:0] Condition,
  output Execute
);

  wire and_1_out, and_2_out, and_3_out, and_4_out, decoder_1_out0, decoder_1_out1, decoder_1_out2,
       decoder_1_out4, decoder_1_out8;

  Decoder #(.select(4)) decoder_1 (
    .out0(decoder_1_out0), .out1(decoder_1_out1), .out2(decoder_1_out2), .out4(decoder_1_out4),
    .out8(decoder_1_out8), .sel(Condition));  // open: out3, out5, out6, out7, out9, out10, out11, out12, out13, out14, out15, en
  and and_1 (and_1_out, decoder_1_out2, C);
  and and_2 (and_2_out, decoder_1_out4, Z);
  and and_3 (and_3_out, decoder_1_out8, N);
  or or_1 (Execute, decoder_1_out0, and_3_out, and_2_out, and_1_out, and_4_out);
  and and_4 (and_4_out, decoder_1_out1, V);
endmodule

module InterruptController (
  input  Call_Clear,
  input  [7:0] InrCode,
  input  [31:0] Value,
  input  Set,
  input  Reset,
  output Handle,
  output [1:0] Type,
  output [5:0] Priority,
  output [23:0] HandleAddress
);

  wire and_1_out, and_2_out, comparator_1_eq, comparator_2_gt, h_q, multiplexer_2_out, not_1_out, not_2_out,
       not_3_out, or_1_out, or_2_out, or_3_out;
  wire [1:0] priority_encoder_1_out;
  wire [7:0] multiplexer_1_out, register_1_q;
  wire [31:0] multiplexer_3_out, ram_1_data;

  Register register_1 (.D(multiplexer_1_out), .en(Call_Clear), .Q(register_1_q), .clk(Call_Clear), .clr(Reset));
  Multiplexer #(.select(2), .width(8)) multiplexer_1 (
    .in0(register_1_q), .in1(InrCode), .in2(InrCode), .in3(InrCode), .out(multiplexer_1_out),
    .sel(priority_encoder_1_out));  // open: en
  and and_1 (and_1_out, or_2_out, Set);
  or or_1 (or_1_out, InrCode[0], InrCode[1], InrCode[2], InrCode[3], InrCode[4]);
  or or_2 (or_2_out, or_1_out, or_3_out);
  or or_3 (or_3_out, InrCode[5], InrCode[6], InrCode[7]);
  Comparator comparator_1 (.a(register_1_q), .b(InrCode), .eq(comparator_1_eq));  // open: gt, lt
  RAM #(.dataWidth(32), .bus("separate")) ram_1 (
    .addr(InrCode), .din(Value), .data(ram_1_data), .str(and_1_out), .clk(and_1_out), .clr(Reset));  // open: sel, ld
  Multiplexer #(.select(2)) multiplexer_2 (
    .in0(h_q), .in1(h_q), .in2(not_1_out), .in3(not_1_out), .out(multiplexer_2_out),
    .sel(priority_encoder_1_out));  // open: en
  Priority_Encoder #(.select(2)) priority_encoder_1 (
    .in0(1'b1), .in1(not_3_out), .in2(comparator_1_eq), .in3(not_1_out), .out(priority_encoder_1_out));
  Multiplexer #(.select(2), .width(32)) multiplexer_3 (
    .in0({Type, Priority, HandleAddress}), .in1(ram_1_data), .in2(ram_1_data), .in3(ram_1_data),
    .out(multiplexer_3_out), .sel(priority_encoder_1_out));  // open: en
  not not_1 (not_1_out, h_q);
  Register #(.width(1)) h (.D(multiplexer_2_out), .en(Call_Clear), .Q(h_q), .clk(Call_Clear), .clr(Reset));
  Register #(.width(32)) register_2 (
    .D(multiplexer_3_out), .en(Call_Clear), .Q({Type, Priority, HandleAddress}), .clk(Call_Clear), .clr(Reset));
  not not_2 (not_2_out, or_2_out);
  Comparator #(.width(6)) comparator_2 (.a(Priority), .b(ram_1_data[29:24]), .gt(comparator_2_gt));  // open: eq, lt
  not not_3 (not_3_out, comparator_2_gt);
  and and_2 (and_2_out, Call_Clear, not_2_out);
  or or_4 (Handle, and_2_out, h_q);
endmodule
